# Fritzing sketch Four_Digital (saved by Fritzing 0.9.3b)
breadboards: 1

parts:
  U1 = 74HC595 [package="DIP16 [THT]"]
  R1 = Resistor [tolerance=±5% resistance=220 package=THT]
  R2 = Resistor [tolerance=±5% resistance=220 package=THT]
  R3 = Resistor [tolerance=±5% resistance=220 package=THT]
  R4 = Resistor [tolerance=±5% resistance=220 package=THT]
  7_Segment_4_Digit_Display1 = 7-SEGMENT-4DIGIT common cathode [part_number=HS420561K-32 package=7-segment-4digit-cathode]
  2560 = Arduino Mega 2560 (Rev3)

nets:
  N1: U1.Q1, 7_Segment_4_Digit_Display1.pin_7
  N2: U1.Q2, 7_Segment_4_Digit_Display1.pin_4
  N3: U1.Q3, 7_Segment_4_Digit_Display1.pin_2
  N4: U1.Q4, 7_Segment_4_Digit_Display1.pin_1
  N5: U1.Q5, 7_Segment_4_Digit_Display1.pin_10
  N6: U1.Q6, 7_Segment_4_Digit_Display1.pin_5
  N7: U1.Q7, 7_Segment_4_Digit_Display1.pin_3
  GND: U1.GND, U1.OE, R1.Pin_0, R2.Pin_0, R3.Pin_0, R4.Pin_0, 2560.GND
  N8: U1.SH_CP, 2560.D10_PWM
  N9: U1.ST_CP, 2560.D9_PWM
  N10: U1.DS, 2560.D8_PWM
  N11: U1.Q0, 7_Segment_4_Digit_Display1.pin_11
  VCC: U1.VCC, 2560.5V
  N12: R1.Pin_1, 7_Segment_4_Digit_Display1.pin_12
  N13: R2.Pin_1, 7_Segment_4_Digit_Display1.pin_9
  N14: R3.Pin_1, 7_Segment_4_Digit_Display1.pin_8
  N15: R4.Pin_1, 7_Segment_4_Digit_Display1.pin_6

custom parts:
  7-SEGMENT-4DIGIT common cathode: A 7 Segment 4 Digit common cathode display, with decimal points
